# Fritzing sketch servoAgitador (saved by Fritzing 0.9.3b)
stripboards: 1

parts:
  U2 = atmega328 [package=dip]
  S2 = Pushbutton [package="[SMD]"]
  C1 = Electrolytic Capacitor [capacitance=10µF voltage=16V package="100 mil [THT, electrolytic]"]
  R1 = Resistor [tolerance=±5% resistance=10k package=THT]
  C2 = Ceramic Capacitor [capacitance=22pF voltage=16V package="100 mil [THT, multilayer]"]
  C3 = Ceramic Capacitor [capacitance=22pF voltage=16V package="100 mil [THT, multilayer]"]
  XTAL1 = Crystal [frequency="16 Mhz" package=THT]
  VCC1 = Battery block 9V
  U3 = Voltage Regulator - 5V [package="TO220 [THT]"]
  C4 = Ceramic Capacitor [capacitance=100nF voltage=16V package="100 mil [THT, multilayer]"]
  J2 = female pin header, 4 pins [form="♀ (female)"]
  LED1 = LED - 3mm [color="Red (633nm)" package="3 mm [THT]"]
  R2 = Resistor [tolerance=±5% resistance=330 package="0805 [SMD]"]
  J3 = Basic Servo
  J4 = male pin header, 3 pins [form="♂ (male)"]

nets:
  N1: U2.RESET, R1.Pin_1, C4.0
  N2: U2.D0_(RX), J2.pin3
  N3: U2.D1_(TX), J2.pin2
  N4: U2.D4, J3.pulse, J4.pin1
  VCC: U2.VCC, U2.AVCC, C1.+, R1.Pin_0, J3.vcc, J4.pin2
  GND: U2.GND, S2.Pin_1, S2.Pin_2, C1.-, C2.0, C3.0, VCC1.-, U3.GND, J2.pin4, R2.Pin_0, J3.gnd, J4.pin3
  N5: U2.XLAT1, C3.1, XTAL1.pin_1
  N6: U2.XLAT2, C2.1, XTAL1.pin_0
  N7: U2.D13, LED1.anode
  N8: S2.Pin_3, S2.Pin_4, C4.1
  N9: VCC1.+, U3.input_voltage, J2.pin1
  N10: LED1.cathode, R2.Pin_1

notes:
  Lista de Materiais
  -----------------------------------
  1 atmega328-pu
  1 push button
  1 resistor 10K
  1 resistor 330R
  1 Cristal 16Mhz
  2 Capacitores 22pF
  1 Capacitor 100nF
  1 Capacitor 10uF
  1 led
  1 Reg. Tensao LM7805
  1 Barra Pinos Femea (4vias)
  ----
  1 Bateria 9v
  1 Servo Motor
  RX-I ==>
  TX-O ==>
  +5V ==>
  GND ==>
  2x 22pF
  10uF
  100nF
  0,1uF
  Opcional
  LM7805
  Resistor
  10K
  330R
  D4
  +
  -

// code stored in the sketch: servoAgitador.ino
#include <Servo.h>
 
#define SERVO 6 // Porta Digital 6 PWM
 
Servo s; // Variavel Servo
int pos; // Posicao Servo
 
void setup ()
{
  s.attach(SERVO);
  Serial.begin(9600);
  s.write(0); // Inicia motor posicao zero
}
 
void loop()
{
  for(pos = 0; pos < 90; pos++)
  {
    s.write(pos);
  delay(15);
  }
delay(1000);
  for(pos = 90; pos >= 0; pos--)
  {
    s.write(pos);
    delay(15);
  }
}
